// Logisim project ALU.circ as structural Verilog: 6 circuits, main circuit SR Latch
module SR_Latch (
  input  in_1,
  input  in_2,
  output out_3,
  output out_4
);

  nor nor_1 (out_3, in_1, out_4);
  nor nor_2 (out_4, out_3, in_2);
endmodule

module D_Latch (
  input  Data,
  input  Write,
  output out_3,
  output out_4
);

  wire and_1_out, and_2_out, not_1_out;

  not not_1 (not_1_out, Data);
  and and_1 (and_1_out, Data, Write);
  and and_2 (and_2_out, not_1_out, Write);
  SR_Latch sr_latch_1 (.in_1(and_1_out), .in_2(and_2_out), .out_3(out_3), .out_4(out_4));
endmodule

module D_flip_flop (
  input  in_1,
  input  in_2,
  output out_3,
  output out_4
);

  wire and_1_out, and_2_out, not_1_out;

  not not_1 (not_1_out, in_1);
  and and_1 (and_1_out, in_1, in_2);
  and and_2 (and_2_out, in_2, not_1_out);
  nand nand_1 (out_3, and_1_out, out_4);
  nand nand_2 (out_4, out_3, and_2_out);
endmodule

module Full_adder (
  input  A,
  input  B,
  input  Cin,
  output S,
  output C_out
);

  wire and_1_out, and_2_out, xor_1_out;

  xor xor_1 (xor_1_out, A, B);
  xor xor_2 (S, xor_1_out, Cin);
  and and_1 (and_1_out, xor_1_out, Cin);
  and and_2 (and_2_out, A, B);
  or or_1 (C_out, and_1_out, and_2_out);
endmodule

module _4_bit_adder (
  input  in_1,
  input  in_2,
  input  in_3,
  input  in_4,
  input  in_5,
  input  in_6,
  input  in_7,
  input  in_8,
  input  in_9,
  output out_10,
  output out_11,
  output out_12,
  output out_13,
  output out_14
);

  wire full_adder_1_c_out, full_adder_2_c_out, full_adder_3_c_out;

  Full_adder full_adder_1 (.A(in_4), .B(in_8), .Cin(in_9), .S(out_13), .C_out(full_adder_1_c_out));
  Full_adder full_adder_2 (.A(in_3), .B(in_7), .Cin(full_adder_1_c_out), .S(out_12), .C_out(full_adder_2_c_out));
  Full_adder full_adder_3 (.A(in_2), .B(in_6), .Cin(full_adder_2_c_out), .S(out_11), .C_out(full_adder_3_c_out));
  Full_adder full_adder_4 (.A(in_1), .B(in_5), .Cin(full_adder_3_c_out), .S(out_10), .C_out(out_14));
endmodule

module ALU (
  input  in_1,
  input  in_2,
  input  in_3,
  input  in_4,
  input  in_5,
  input  in_6,
  input  in_7,
  input  in_8,
  input  in_9,
  output out_10,
  output out_11,
  output out_12,
  output out_13,
  output out_14,
  output out_15,
  output out_16
);

  wire and_1_out, and_2_out, not_1_out, not_2_out, not_3_out, not_4_out, or_1_out, or_2_out, or_3_out,
       or_4_out;

  or or_1 (or_1_out, in_5, in_9);
  or or_2 (or_2_out, in_6, in_9);
  or or_3 (or_3_out, in_7, in_9);
  or or_4 (or_4_out, in_8, in_9);
  _4_bit_adder u_4_bit_adder_1 (
    .in_1(in_1), .in_2(in_2), .in_3(in_3), .in_4(in_4), .in_5(or_1_out), .in_6(or_2_out), .in_7(or_3_out),
    .in_8(or_4_out), .in_9(in_9), .out_10(out_10), .out_11(out_11), .out_12(out_12), .out_13(out_13),
    .out_14(out_14));
  not not_1 (not_1_out, out_10);
  not not_2 (not_2_out, out_11);
  not not_3 (not_3_out, out_12);
  not not_4 (not_4_out, out_13);
  and and_1 (and_1_out, not_1_out, not_2_out);
  and and_2 (and_2_out, and_1_out, not_3_out);
  and and_3 (out_16, and_2_out, not_4_out);

  assign out_15 = out_10;
endmodule
